# Fritzing sketch devre (saved by Fritzing 0.9.3b)
breadboards: 1

parts:
  sdCard1 = my_sdCard
  DHT11_1 = DHT22_BLACK_PCB
  Parça1 = Arduino Uno (Rev3)

nets:
  GND: sdCard1.GND, DHT11_1.connector6, Parça1.GND
  VCC: sdCard1.VCC, DHT11_1.connector5, Parça1.5V
  N1: sdCard1.MISO, Parça1.D12/MISO
  N2: sdCard1.MOSI, Parça1.D11_PWM/MOSI
  N3: sdCard1.SCK, Parça1.D13/SCK
  N4: sdCard1.CS, Parça1.D10_PWM/SS

custom parts:
  my_sdCard: micro sdCard Adapter with 90º pin header. Use a filtering Capacitor between CS and GND if needed. PCB View Pinouts are Reversed for laying parallel on PCB using a 90º pin header.
